// Logisim project mycirc.circ as structural Verilog: 7 circuits, main circuit intruction_fetcher
module intruction_fetcher (
  input  [31:0] next_PC,
  input  write,
  input  clk,
  output [31:0] PC_4,
  output [31:0] instruction
);

  wire [31:0] PC_q;

  Register #(.width(32)) PC (.D(next_PC), .en(write), .clk(clk), .Q(PC_q), .clr(PC_q[26]));
  ROM #(.addrWidth(24), .dataWidth(32)) InstructionMemory (.addr(PC_q[25:2]), .data(instruction));
  Adder #(.width(32)) adder_1 (.a(PC_q), .b(32'h4), .out(PC_4), .cin(1'b0));  // open: cout

  // Notes on the sheet:
  //   contents of InstructionMemory (hex, n*v repeats v):
  //   16777208*0 11110000 11010000 10101100 110000
endmodule

module registers (
  input  [4:0] r_reg_1,
  input  [4:0] r_reg_0,
  input  wr_enable,
  input  ck,
  input  [4:0] wr_addr,
  input  [31:0] in_6,
  input  ck_2,
  output [31:0] reg_out_0,
  output [31:0] reg_out_1
);

  wire demultiplexer_1_p1, demultiplexer_2_out0, demultiplexer_2_out1, demultiplexer_2_out2,
       demultiplexer_2_out3, demultiplexer_2_out4, demultiplexer_2_out5, demultiplexer_2_out6,
       demultiplexer_2_out7, demultiplexer_2_out8, demultiplexer_2_out9, demultiplexer_2_out10,
       demultiplexer_2_out11, demultiplexer_2_out12, demultiplexer_2_out13, demultiplexer_2_out14,
       demultiplexer_2_out15, demultiplexer_2_out16, demultiplexer_2_out17, demultiplexer_2_out18,
       demultiplexer_2_out19, demultiplexer_2_out20, demultiplexer_2_out21, demultiplexer_2_out22,
       demultiplexer_2_out23, demultiplexer_2_out24, demultiplexer_2_out25, demultiplexer_2_out26,
       demultiplexer_2_out27, demultiplexer_2_out28, demultiplexer_2_out29, demultiplexer_2_out30,
       demultiplexer_2_out31, register_20_p1, register_21_p5, register_22_p1, undriven_2, undriven_3,
       undriven_4, undriven_5, undriven_14, undriven_15, undriven_16, undriven_23;
  wire [31:0] data_q, reg_out_1_q, register_1_q, register_2_q, register_4_q, register_5_q, register_6_q,
       register_7_q, register_8_q, register_9_q, register_10_q, register_17_q, register_18_q, register_21_p7,
       undriven, undriven_6, undriven_7, undriven_8, undriven_9, undriven_10, undriven_11, undriven_12,
       undriven_13, undriven_17, undriven_18, undriven_19, undriven_20, undriven_21, undriven_22,
       undriven_24, undriven_25, undriven_26, undriven_27, undriven_28, undriven_29;

  // Demultiplexer #(.select(5), .enable("false")) demultiplexer_1: pin names not known; wires that end beside it: demultiplexer_1_p1
  Demultiplexer #(.select(5), .enable("false")) demultiplexer_2 (
    .out0(demultiplexer_2_out0), .out1(demultiplexer_2_out1), .out2(demultiplexer_2_out2),
    .out3(demultiplexer_2_out3), .out4(demultiplexer_2_out4), .out5(demultiplexer_2_out5),
    .out6(demultiplexer_2_out6), .out7(demultiplexer_2_out7), .out8(demultiplexer_2_out8),
    .out9(demultiplexer_2_out9), .out10(demultiplexer_2_out10), .out11(demultiplexer_2_out11),
    .out12(demultiplexer_2_out12), .out13(demultiplexer_2_out13), .out14(demultiplexer_2_out14),
    .out15(demultiplexer_2_out15), .out16(demultiplexer_2_out16), .out17(demultiplexer_2_out17),
    .out18(demultiplexer_2_out18), .out19(demultiplexer_2_out19), .out20(demultiplexer_2_out20),
    .out21(demultiplexer_2_out21), .out22(demultiplexer_2_out22), .out23(demultiplexer_2_out23),
    .out24(demultiplexer_2_out24), .out25(demultiplexer_2_out25), .out26(demultiplexer_2_out26),
    .out27(demultiplexer_2_out27), .out28(demultiplexer_2_out28), .out29(demultiplexer_2_out29),
    .out30(demultiplexer_2_out30), .out31(demultiplexer_2_out31), .in(wr_enable), .sel(wr_addr));
  Register #(.width(32)) register_1 (.D(in_6), .en(demultiplexer_2_out0), .clk(ck_2), .Q(register_1_q), .clr(1'b1));
  Register #(.width(32)) register_2 (
    .D(undriven), .en(undriven_2), .Q(register_2_q), .clk(undriven_3), .clr(undriven_4));
  Register #(.width(32)) register_3 (
    .D(undriven), .en(undriven_2), .Q(register_2_q), .clk(undriven_3), .clr(undriven_4));
  Register #(.width(32)) register_4 (.D(in_6), .en(demultiplexer_2_out2), .clk(ck_2), .Q(register_4_q), .clr(1'b0));
  Register #(.width(32)) register_5 (.D(in_6), .en(demultiplexer_2_out3), .clk(ck_2), .Q(register_5_q), .clr(1'b0));
  Register #(.width(32)) register_6 (
    .D(in_6), .en(demultiplexer_2_out4), .clk(ck_2), .Q(register_6_q), .clr(undriven_5));
  Register #(.width(32)) register_7 (.D(in_6), .en(demultiplexer_2_out6), .clk(ck_2), .Q(register_7_q), .clr(1'b0));
  Register #(.width(32)) register_8 (.D(in_6), .en(demultiplexer_2_out7), .clk(ck_2), .Q(register_8_q), .clr(1'b0));
  Register #(.width(32)) register_9 (.D(in_6), .en(demultiplexer_2_out9), .clk(ck_2), .Q(register_9_q), .clr(1'b0));
  Register #(.width(32)) register_10 (.D(in_6), .en(demultiplexer_2_out15), .clk(ck_2), .Q(register_10_q), .clr(1'b0));
  Register #(.width(32)) register_11 ();  // open: D, en, clk, Q, clr
  // Register #(.width(32)) register_12: pin names not known; wires that end beside it: 1'b0
  // Register #(.width(32)) register_13: pin names not known; wires that end beside it: 1'b0
  // Register #(.width(32)) register_14: pin names not known; wires that end beside it: 1'b0
  // Register #(.width(32)) register_15: pin names not known; wires that end beside it: 1'b0
  // Register #(.width(32)) register_16: pin names not known
  Register #(.width(32)) data (.D(in_6), .en(demultiplexer_2_out18), .clk(ck_2), .Q(data_q), .clr(undriven_14));
  Register #(.width(32)) register_17 (
    .D(in_6), .en(demultiplexer_2_out19), .clk(ck_2), .Q(register_17_q), .clr(undriven_15));
  Register #(.width(32)) register_18 (
    .D(in_6), .en(demultiplexer_2_out21), .clk(ck_2), .Q(register_18_q), .clr(undriven_16));
  Register #(.width(32)) register_19 ();  // open: D, en, Q, clk, clr
  // Register #(.width(32)) register_20: pin names not known; wires that end beside it: register_20_p1, demultiplexer_2_out24
  // Register #(.width(32)) register_21: pin names not known; wires that end beside it: ck_2, register_20_p1, demultiplexer_2_out28, 1'b0, register_21_p5, register_21_p5, register_21_p7
  // Register #(.width(32)) register_22: pin names not known; wires that end beside it: register_22_p1
  Register #(.width(32)) u_reg_out_1 (
    .D(undriven_22), .en(demultiplexer_2_out29), .clk(ck_2), .Q(reg_out_1_q), .clr(undriven_23));
  // Register #(.width(32)) register_23: pin names not known
  // Register #(.width(32)) register_24: pin names not known
  Register #(.width(32)) register_25 ();  // open: D, en, Q, clk, clr
  Register #(.width(32)) register_26 ();  // open: D, en, Q, clk, clr
  Register #(.width(32)) register_27 ();  // open: D, en, Q, clk, clr
  Register #(.width(32)) register_28 ();  // open: D, en, Q, clk, clr
  Register #(.width(32)) register_29 ();  // open: D, en, Q, clk, clr
  Multiplexer #(.select(5), .width(32), .enable("false")) multiplexer_1 (
    .in0(register_1_q), .in1(undriven_6), .in2(register_4_q), .in3(register_5_q), .in4(register_6_q),
    .in5(undriven_7), .in6(register_7_q), .in7(register_8_q), .in8(undriven_8), .in9(register_9_q),
    .in10(undriven_11), .in11(undriven_12), .in12(undriven_13), .in13(undriven_9), .in14(undriven_10),
    .in15(register_10_q), .in16(undriven_17), .in17(undriven_20), .in18(data_q), .in19(register_17_q),
    .in20(undriven_21), .in21(register_18_q), .in22(undriven_18), .in23(undriven_19), .in24(undriven_24),
    .in25(undriven_25), .in26(undriven_26), .in27(undriven_29), .in28(register_21_p7), .in29(reg_out_1_q),
    .in30(undriven_27), .in31(undriven_28), .out(reg_out_0), .sel(r_reg_0));
  Multiplexer #(.select(5), .width(32), .enable("false")) multiplexer_2 (
    .in0(register_1_q), .in1(undriven_6), .in2(register_4_q), .in3(register_5_q), .in4(register_6_q),
    .in5(undriven_7), .in6(register_7_q), .in7(register_8_q), .in8(undriven_8), .in9(register_9_q),
    .in10(undriven_11), .in11(undriven_12), .in12(undriven_13), .in13(undriven_9), .in14(undriven_10),
    .in15(register_10_q), .in16(undriven_17), .in17(undriven_20), .in18(data_q), .in19(register_17_q),
    .in20(undriven_21), .in21(register_18_q), .in22(undriven_18), .in23(undriven_19), .in24(undriven_24),
    .in25(undriven_25), .in26(undriven_26), .in27(undriven_29), .in28(register_21_p7), .in29(reg_out_1_q),
    .in30(undriven_27), .in31(undriven_28), .out(reg_out_1), .sel(r_reg_1));
  Multiplexer #(.select(5), .width(32), .enable("false")) multiplexer_3 ();  // open: in0, in1, in2, in3, in4, in5, in6, in7, in8, in9, in10, in11, in12, in13, in14, in15, in16, in17, in18, in19, in20, in21, in22, in23, in24, in25, in26, in27, in28, in29, in30, in31, out, sel
endmodule

module ALU (
  input  [31:0] ALU_in0,
  input  [31:0] ALU_in1,
  input  [2:0] ALU_op,
  output [31:0] ALU_out,
  output is_0
);

  wire [31:0] adder_1_out, and_1_out, nor_1_out, or_1_out, subtractor_1_out;

  Adder #(.width(32)) adder_1 (.a(ALU_in0), .b(ALU_in1), .out(adder_1_out), .cin(1'b0));  // open: cout
  Subtractor #(.width(32)) subtractor_1 (.a(ALU_in0), .b(ALU_in1), .out(subtractor_1_out), .bin(1'b0));  // open: bout
  assign and_1_out = ALU_in0 & ALU_in1;  // AND_Gate and_1, 32 bits wide
  assign or_1_out = ALU_in0 | ALU_in1;  // OR_Gate or_1, 32 bits wide
  assign nor_1_out = ~(ALU_in0 | ALU_in1);  // NOR_Gate nor_1, 32 bits wide
  Multiplexer #(.select(3), .width(32), .enable("false")) multiplexer_1 (
    .in0(adder_1_out), .in1(subtractor_1_out), .in2(and_1_out), .in3(or_1_out), .in4(nor_1_out),
    .out(ALU_out), .sel(ALU_op));  // open: in5, in6, in7
  nor nor_2 (is_0, ALU_out[0], ALU_out[1], ALU_out[2], ALU_out[3], ALU_out[4], ALU_out[5], ALU_out[6], ALU_out[7], ALU_out[8], ALU_out[9], ALU_out[10], ALU_out[11], ALU_out[12], ALU_out[13], ALU_out[14], ALU_out[15], ALU_out[17], ALU_out[18], ALU_out[19], ALU_out[20], ALU_out[21], ALU_out[22], ALU_out[23], ALU_out[24], ALU_out[25], ALU_out[26], ALU_out[27], ALU_out[28], ALU_out[29], ALU_out[30], ALU_out[31], ALU_out[16]);
endmodule

module main (
  input  clk,
  input  in_2,
  input  in_3,
  input  write,
  input  in_5,
  input  in_6,
  input  [1:0] in_7,
  input  in_8,
  input  [2:0] alu_op,
  input  in_10,
  input  in_11,
  output is_0
);

  wire [4:0] multiplexer_1_out;
  wire [31:0] adder_1_out, alu_1_alu_out, data_memory_1_out_7, intruction_fetcher_1_instruction,
       intruction_fetcher_1_pc_4, multiplexer_2_out, multiplexer_3_out, multiplexer_4_out,
       registers_1_reg_out_0, registers_1_reg_out_1, shift_2_1_shift_out, signal_extender_1_sigextout;

  // Probe on multiplexer_3_out
  // Probe on intruction_fetcher_1_instruction
  intruction_fetcher intruction_fetcher_1 (
    .next_PC(multiplexer_3_out), .write(write), .clk(clk), .PC_4(intruction_fetcher_1_pc_4),
    .instruction(intruction_fetcher_1_instruction));
  // Probe on intruction_fetcher_1_instruction[25:21]
  // Probe on intruction_fetcher_1_instruction[20:16]
  Multiplexer #(.width(5), .enable("false")) multiplexer_1 (
    .in0(intruction_fetcher_1_instruction[20:16]), .in1(intruction_fetcher_1_instruction[15:11]),
    .out(multiplexer_1_out), .sel(in_11));
  // Probe on multiplexer_4_out
  // Probe on multiplexer_1_out
  signal_extender signal_extender_1 (
    .sigextin(intruction_fetcher_1_instruction[15:0]), .sigextout(signal_extender_1_sigextout));
  registers registers_1 (
    .reg_out_0(registers_1_reg_out_0), .in_6(multiplexer_4_out), .wr_enable(in_5),
    .r_reg_1(intruction_fetcher_1_instruction[20:16]), .r_reg_0(intruction_fetcher_1_instruction[25:21]),
    .wr_addr(multiplexer_1_out), .ck_2(clk), .reg_out_1(registers_1_reg_out_1));
  // Probe on registers_1_reg_out_0
  // Probe on registers_1_reg_out_1
  shift_2 shift_2_1 (.Shift_In(signal_extender_1_sigextout), .Shift_Out(shift_2_1_shift_out));
  Multiplexer #(.width(32), .enable("false")) multiplexer_2 (
    .in0(registers_1_reg_out_1), .in1(signal_extender_1_sigextout), .out(multiplexer_2_out), .sel(in_3));
  Adder #(.width(32)) adder_1 (
    .a(intruction_fetcher_1_pc_4), .b(shift_2_1_shift_out), .out(adder_1_out), .cin(1'b0));  // open: cout
  Multiplexer #(.width(32), .enable("false")) multiplexer_3 (
    .in0(intruction_fetcher_1_pc_4), .in1(adder_1_out), .out(multiplexer_3_out), .sel(in_2));
  ALU alu_1 (
    .ALU_in0(registers_1_reg_out_0), .ALU_in1(multiplexer_2_out), .ALU_op(alu_op), .ALU_out(alu_1_alu_out),
    .is_0(is_0));
  // Probe on alu_1_alu_out
  data_memory data_memory_1 (
    .addr(alu_1_alu_out), .data(registers_1_reg_out_1), .write_en(in_6), .whb(in_7), .read(in_10), .clk(clk),
    .out_7(data_memory_1_out_7));
  Multiplexer #(.width(32), .enable("false")) multiplexer_4 (
    .in0(data_memory_1_out_7), .in1(alu_1_alu_out), .out(multiplexer_4_out), .sel(in_8));
endmodule

module data_memory (
  input  [31:0] addr,
  input  [31:0] data,
  input  write_en,
  input  [1:0] whb,
  input  read,
  input  clk,
  output [31:0] out_7
);

  wire [1:0] demultiplexer_1_out0, demultiplexer_1_out1;
  wire [3:0] demultiplexer_2_out0, multiplexer_2_out;
  wire [7:0] demultiplexer_4_out0, demultiplexer_4_out1, demultiplexer_4_out2, demultiplexer_4_out3,
       multiplexer_4_out, ram_1_dout, ram_2_dout, ram_3_dout, ram_4_dout;
  wire [15:0] demultiplexer_3_out0, demultiplexer_3_out1, multiplexer_3_out;
  wire [31:0] multiplexer_1_out;

  Demultiplexer #(.width(2), .enable("false")) demultiplexer_1 (
    .out0(demultiplexer_1_out0), .out1(demultiplexer_1_out1), .in({2{write_en}}), .sel(addr[1]));
  Demultiplexer #(.select(2), .enable("false")) demultiplexer_2 (
    .out0(demultiplexer_2_out0[0]), .out1(demultiplexer_2_out0[1]), .out2(demultiplexer_2_out0[2]),
    .out3(demultiplexer_2_out0[3]), .in(write_en), .sel({addr[0], addr[1]}));
  Demultiplexer #(.width(16), .enable("false")) demultiplexer_3 (
    .out0(demultiplexer_3_out0), .out1(demultiplexer_3_out1), .in(data[15:0]), .sel(addr[1]));
  Demultiplexer #(.select(2), .width(8), .enable("false")) demultiplexer_4 (
    .out0(demultiplexer_4_out0), .out1(demultiplexer_4_out1), .out2(demultiplexer_4_out2),
    .out3(demultiplexer_4_out3), .in(data[7:0]), .sel({addr[0], addr[1]}));
  Multiplexer #(.select(2), .width(32), .enable("false")) multiplexer_1 (
    .in0(data), .in1({demultiplexer_3_out1, demultiplexer_3_out0}),
    .in2({demultiplexer_4_out3, demultiplexer_4_out2, demultiplexer_4_out1, demultiplexer_4_out0}),
    .out(multiplexer_1_out), .sel(whb));  // open: in3
  Multiplexer #(.select(2), .width(4), .enable("false")) multiplexer_2 (
    .in0({4{write_en}}), .in1({demultiplexer_1_out1, demultiplexer_1_out0}), .in2(demultiplexer_2_out0),
    .out(multiplexer_2_out), .sel(whb));  // open: in3
  // Probe on addr[25:2]
  RAM #(.addrWidth(24), .databus("bibus")) ram_1 (
    .addr(addr[25:2]), .we(multiplexer_2_out[0]), .oe(read), .clk(clk), .din(multiplexer_1_out[7:0]),
    .dout(ram_1_dout));
  RAM #(.addrWidth(24), .databus("bibus")) ram_2 (
    .addr(addr[25:2]), .we(multiplexer_2_out[1]), .oe(read), .clk(clk), .din(multiplexer_1_out[15:8]),
    .dout(ram_2_dout));
  RAM #(.addrWidth(24), .databus("bibus")) ram_3 (
    .addr(addr[25:2]), .we(multiplexer_2_out[2]), .oe(read), .clk(clk), .din(multiplexer_1_out[23:16]),
    .dout(ram_3_dout));
  RAM #(.addrWidth(24), .databus("bibus")) ram_4 (
    .addr(addr[25:2]), .we(multiplexer_2_out[3]), .oe(read), .clk(clk), .din(multiplexer_1_out[31:24]),
    .dout(ram_4_dout));
  // Probe on ram_1_dout
  // Probe on ram_2_dout
  // Probe on ram_3_dout
  // Probe on ram_4_dout
  Multiplexer #(.width(16), .enable("false")) multiplexer_3 (
    .in0({ram_2_dout, ram_1_dout}), .in1({ram_4_dout, ram_3_dout}), .out(multiplexer_3_out), .sel(addr[0]));
  Multiplexer #(.select(2), .width(8), .enable("false")) multiplexer_4 (
    .in0(ram_1_dout), .in1(ram_2_dout), .in2(ram_3_dout), .in3(ram_4_dout), .out(multiplexer_4_out),
    .sel(addr[1:0]));
  Multiplexer #(.select(2), .width(32), .enable("false")) multiplexer_5 (
    .in0({ram_4_dout, ram_3_dout, ram_2_dout, ram_1_dout}), .in1({{24{1'b0}}, multiplexer_4_out}),
    .in2({{16{1'b0}}, multiplexer_3_out}), .out(out_7), .sel(whb));  // open: in3
endmodule

module signal_extender (
  input  [15:0] sigextin,
  output [31:0] sigextout
);


  assign sigextout = {{17{sigextin[15]}}, sigextin[14:0]};
endmodule

module shift_2 (
  input  [31:0] Shift_In,
  output [31:0] Shift_Out
);


  assign Shift_Out = {Shift_In[29:0], 2'b00};
endmodule
